# Fritzing sketch nrf24l01 Arduino Nano (saved by Fritzing 0.9.1b)
breadboards: 1

parts:
  Part1 = Arduino Nano (Rev3.0)
  NRF24L1 = NRF24L01
  LED1 = LED - 5mm [color="Red (633nm)" package="5 mm [THT]"]

nets:
  GND: Part1.GND, NRF24L1.GND, LED1.anode
  N1: Part1.D2, LED1.cathode
  N2: Part1.D9, NRF24L1.CE
  N3: Part1.D10, NRF24L1.CSN
  N4: Part1.D11/MOSI, NRF24L1.SCK
  N5: Part1.D12/MISO, NRF24L1.MISO
  3V3: Part1.3V3, NRF24L1.VCC
  N6: Part1.D13/SCK, NRF24L1.MOSI

custom parts:
  NRF24L01: NRF24L01 module
