# Fritzing sketch nrf24l01 RPi (saved by Fritzing 0.9.1b)

parts:
  NRF24L1 = NRF24L01
  Raspberry_Pi1 = Raspberry Pi B rev2

nets:
  VCC: NRF24L1.VCC, Raspberry_Pi1.3V3
  N1: NRF24L1.CSN, Raspberry_Pi1.GPIO_8
  N2: NRF24L1.MOSI, Raspberry_Pi1.GPIO_10
  N3: NRF24L1.IRQ, Raspberry_Pi1.GPIO_9
  GND: NRF24L1.GND, Raspberry_Pi1.GND
  N4: NRF24L1.CE, Raspberry_Pi1.GPIO_25
  N5: NRF24L1.SCK, Raspberry_Pi1.GPIO_11

custom parts:
  NRF24L01: NRF24L01 module
